// Logisim project project.circ as structural Verilog: 17 circuits, main circuit main
module main (
  input  Reset
);

  wire ALU_out_5, clock_1_out, control_out_4, control_out_6, control_out_7, control_out_8, control_out_11,
       ext_op, MemtoReg, RegDst;
  wire [2:0] control_out_10;
  wire [4:0] multiplexer_1_out;
  wire [7:0] DM_out_5, DM_out_5_2, DM_out_5_3, DM_out_5_4, multiplexer_5_out;
  wire [31:0] ALU_out_4, bit_extender_1_out, EXT_out_3, IFU_out_5, multiplexer_2_out, multiplexer_3_out,
       multiplexer_4_out, RegFile_out_7, RegFile_out_8;

  Clock clock_1 (.out(clock_1_out));
  // Probe on IFU_out_5
  IFU IFU (.out_5(IFU_out_5), .CLK(clock_1_out), .Reset(Reset), .BR(control_out_8), .Zero(ALU_out_5));
  Multiplexer #(.width(5), .enable("false")) multiplexer_1 (
    .in0(IFU_out_5[20:16]), .in1(IFU_out_5[15:11]), .out(multiplexer_1_out), .sel(RegDst));
  control control (
    .in_1(IFU_out_5[31:26]), .in_2(IFU_out_5[5:0]), .out_3(RegDst), .out_4(control_out_4), .out_5(MemtoReg),
    .out_6(control_out_6), .out_7(control_out_7), .out_8(control_out_8), .out_9(ext_op),
    .out_10(control_out_10), .out_11(control_out_11));
  RegFile RegFile (
    .in_3(IFU_out_5[25:21]), .in_4(IFU_out_5[20:16]), .in_5(multiplexer_1_out), .in_6(multiplexer_3_out),
    .Clk(clock_1_out), .RegWr(control_out_6), .out_7(RegFile_out_7), .out_8(RegFile_out_8));
  \EXT_16到32  EXT (.in_1(IFU_out_5[15:0]), .in_2(ext_op), .out_3(EXT_out_3));
  Multiplexer #(.width(32), .enable("false")) multiplexer_2 (
    .in0(RegFile_out_8), .in1(EXT_out_3), .out(multiplexer_2_out), .sel(control_out_4));
  Multiplexer #(.width(32), .enable("false")) multiplexer_3 (
    .in0(ALU_out_4), .in1(multiplexer_4_out), .out(multiplexer_3_out), .sel(MemtoReg));
  ALU ALU (.in_2(RegFile_out_7), .in_3(multiplexer_2_out), .in_1(control_out_10), .out_4(ALU_out_4), .out_5(ALU_out_5));
  DM DM (
    .in_3(ALU_out_4[6:2]), .in_4(RegFile_out_8), .CLK(clock_1_out), .MemWrite(control_out_7),
    .out_5({DM_out_5_4, DM_out_5_3, DM_out_5_2, DM_out_5}));
  Multiplexer #(.width(32), .enable("false")) multiplexer_4 (
    .in0({DM_out_5_4, DM_out_5_3, DM_out_5_2, DM_out_5}), .in1(bit_extender_1_out), .out(multiplexer_4_out),
    .sel(control_out_11));
  Multiplexer #(.select(2), .width(8), .enable("false")) multiplexer_5 (
    .in0(DM_out_5), .in1(DM_out_5_2), .in2(DM_out_5_3), .in3(DM_out_5_4), .out(multiplexer_5_out),
    .sel(ALU_out_4[1:0]));
  assign bit_extender_1_out = {{24{multiplexer_5_out[7]}}, multiplexer_5_out};  // Bit_Extender bit_extender_1
endmodule

module IFU (
  input  CLK,
  input  Reset,
  input  BR,
  input  Zero,
  output [31:0] out_5
);

  wire [29:0] npc_1_out_6;

  NPC npc_1 (.in_1(out_5[15:0]), .in_2(CLK), .CLEAR(Reset), .BR(BR), .ZERO(Zero), .out_6(npc_1_out_6));
  ROM #(.addrWidth(5), .dataWidth(32)) rom_1 (.addr(npc_1_out_6[4:0]), .data(out_5));  // open: sel

  // Notes on the sheet:
  //   contents of rom_1 (hex, n*v repeats v):
  //   80220000
endmodule

module ADD (
  input  X,
  input  Y,
  input  C0,
  output S,
  output C1
);

  wire and_1_out, and_2_out, and_3_out, xor_1_out;

  xor xor_1 (xor_1_out, X, Y);
  and and_1 (and_1_out, X, Y);
  and and_2 (and_2_out, Y, C0);
  and and_3 (and_3_out, C0, X);
  xor xor_2 (S, xor_1_out, C0);
  or or_1 (C1, and_1_out, and_2_out, and_3_out);
endmodule

module AADD (
  input  [7:0] in_1,
  input  [7:0] in_2,
  input  in_3,
  output [7:0] out_4,
  output out_5
);

  wire add_1_c1, add_2_c1, add_3_c1, add_4_c1, add_5_c1, add_6_c1, add_7_c1;

  ADD add_1 (.X(in_1[0]), .Y(in_2[0]), .C0(in_3), .S(out_4[0]), .C1(add_1_c1));
  ADD add_2 (.X(in_1[1]), .Y(in_2[1]), .C0(add_1_c1), .S(out_4[1]), .C1(add_2_c1));
  ADD add_3 (.X(in_1[2]), .Y(in_2[2]), .C0(add_2_c1), .S(out_4[2]), .C1(add_3_c1));
  ADD add_4 (.X(in_1[3]), .Y(in_2[3]), .C0(add_3_c1), .S(out_4[3]), .C1(add_4_c1));
  ADD add_5 (.X(in_1[4]), .Y(in_2[4]), .C0(add_4_c1), .S(out_4[4]), .C1(add_5_c1));
  ADD add_6 (.X(in_1[5]), .Y(in_2[5]), .C0(add_5_c1), .S(out_4[5]), .C1(add_6_c1));
  ADD add_7 (.X(in_1[6]), .Y(in_2[6]), .C0(add_6_c1), .S(out_4[6]), .C1(add_7_c1));
  ADD add_8 (.X(in_1[7]), .Y(in_2[7]), .C0(add_7_c1), .S(out_4[7]), .C1(out_5));
endmodule

module AAADD (
  input  [31:0] in_1,
  input  [31:0] in_2,
  output [31:0] out_3,
  output out_4
);

  wire aadd_1_out_5, aadd_2_out_5, aadd_4_out_5;

  AADD aadd_1 (.in_1(in_1[15:8]), .in_2(in_2[15:8]), .in_3(aadd_4_out_5), .out_4(out_3[15:8]), .out_5(aadd_1_out_5));
  AADD aadd_2 (.in_1(in_1[23:16]), .in_2(in_2[23:16]), .in_3(aadd_1_out_5), .out_4(out_3[23:16]), .out_5(aadd_2_out_5));
  AADD aadd_3 (.in_1(in_1[31:24]), .in_2(in_2[31:24]), .in_3(aadd_2_out_5), .out_4(out_3[31:24]), .out_5(out_4));
  AADD aadd_4 (.in_1(in_1[7:0]), .in_2(in_2[7:0]), .in_3(1'b0), .out_4(out_3[7:0]), .out_5(aadd_4_out_5));
endmodule

module PC (
  input  CLK,
  input  CLEAR,
  input  [29:0] in_3,
  output [29:0] out_4
);

  wire [7:6] \d寄存器_8位_4_out_5 ;

  \D寄存器_8位  \d寄存器_8位_1  (.clk(CLK), .en(1'b1), .clear(CLEAR), .in_4(in_3[7:0]), .out_5(out_4[7:0]));
  \D寄存器_8位  \d寄存器_8位_2  (.clk(CLK), .en(1'b1), .clear(CLEAR), .in_4(in_3[15:8]), .out_5(out_4[15:8]));
  \D寄存器_8位  \d寄存器_8位_3  (.clk(CLK), .en(1'b1), .clear(CLEAR), .in_4(in_3[23:16]), .out_5(out_4[23:16]));
  \D寄存器_8位  \d寄存器_8位_4  (
    .clk(CLK), .en(1'b1), .clear(CLEAR), .in_4({2'b00, in_3[29:24]}),
    .out_5({\d寄存器_8位_4_out_5 , out_4[29:24]}));

  // Notes on the sheet:
  //   EN
endmodule

module \D寄存器_8位  (
  input  clk,
  input  en,
  input  clear,
  input  [7:0] in_4,
  output [7:0] out_5
);

  D_Flip_Flop d_ff_1 (.clk(clk), .D(in_4[0]), .Q(out_5[0]), .en(en), .reset(clear));  // open: Qn, preset
  D_Flip_Flop d_ff_2 (.clk(clk), .D(in_4[1]), .Q(out_5[1]), .en(en), .reset(clear));  // open: Qn, preset
  D_Flip_Flop d_ff_3 (.clk(clk), .D(in_4[2]), .Q(out_5[2]), .en(en), .reset(clear));  // open: Qn, preset
  D_Flip_Flop d_ff_4 (.clk(clk), .D(in_4[3]), .Q(out_5[3]), .en(en), .reset(clear));  // open: Qn, preset
  D_Flip_Flop d_ff_5 (.clk(clk), .D(in_4[4]), .Q(out_5[4]), .en(en), .reset(clear));  // open: Qn, preset
  D_Flip_Flop d_ff_6 (.clk(clk), .D(in_4[5]), .Q(out_5[5]), .en(en), .reset(clear));  // open: Qn, preset
  D_Flip_Flop d_ff_7 (.clk(clk), .D(in_4[6]), .Q(out_5[6]), .en(en), .reset(clear));  // open: Qn, preset
  D_Flip_Flop d_ff_8 (.clk(clk), .D(in_4[7]), .Q(out_5[7]), .en(en), .reset(clear));  // open: Qn, preset
endmodule

module NPC (
  input  [15:0] in_1,
  input  in_2,
  input  CLEAR,
  input  BR,
  input  ZERO,
  output [29:0] out_6
);

  wire and_1_out;
  wire [29:0] bit_extender_1_out, multiplexer_1_out;
  wire [31:0] aaadd_1_out_3, aaadd_2_out_3, bit_extender_2_out, bit_extender_3_out, bit_extender_4_out;
  wire [31:30] multiplexer_1_out_2;

  assign bit_extender_1_out = {{14{in_1[15]}}, in_1};  // Bit_Extender bit_extender_1
  and and_1 (and_1_out, BR, ZERO);
  assign bit_extender_2_out = {{2{1'b0}}, bit_extender_1_out};  // Bit_Extender bit_extender_2
  Multiplexer #(.width(32), .enable("false")) multiplexer_1 (
    .in0(aaadd_2_out_3), .in1(aaadd_1_out_3), .out({multiplexer_1_out_2, multiplexer_1_out}), .sel(and_1_out));
  AAADD aaadd_1 (.in_1(aaadd_2_out_3), .in_2(bit_extender_2_out), .out_3(aaadd_1_out_3));  // open: out_4
  PC pc_1 (.CLK(in_2), .CLEAR(CLEAR), .in_3(multiplexer_1_out), .out_4(out_6));
  AAADD aaadd_2 (.in_1(bit_extender_4_out), .in_2(bit_extender_3_out), .out_3(aaadd_2_out_3));  // open: out_4
  assign bit_extender_3_out = {{2{1'b0}}, out_6};  // Bit_Extender bit_extender_3
  assign bit_extender_4_out = {{31{1'b0}}, 1'b1};  // Bit_Extender bit_extender_4

  // Notes on the sheet:
  //   IMM
  //   CLK
endmodule

module \EXT_16到32  (
  input  [15:0] in_1,
  input  in_2,
  output [31:0] out_3
);

  wire [31:0] bit_extender_1_out, bit_extender_2_out;

  assign bit_extender_1_out = {{16{1'b0}}, in_1};  // Bit_Extender bit_extender_1
  assign bit_extender_2_out = {{16{in_1[15]}}, in_1};  // Bit_Extender bit_extender_2
  Multiplexer #(.width(32), .enable("false")) multiplexer_1 (
    .in0(bit_extender_1_out), .in1(bit_extender_2_out), .out(out_3), .sel(in_2));

  // Notes on the sheet:
  //   A
  //   c
  //   B
endmodule

module RegFile (
  input  Clk,
  input  RegWr,
  input  [4:0] in_3,
  input  [4:0] in_4,
  input  [4:0] in_5,
  input  [31:0] in_6,
  output [31:0] out_7,
  output [31:0] out_8
);

  \Reg_32个  \reg_32个_1  (
    .in_3(in_3), .in_4(in_4), .in_5(in_5), .in_6(in_6), .RegWr(RegWr), .Clk(Clk), .out_7(out_7), .out_8(out_8));

  // Notes on the sheet:
  //   RS1
  //   RS2
  //   RD
  //   WData
  //   RD1
  //   RD2
endmodule

module Reg (
  input  RegWr,
  input  Clk,
  input  [7:0] in_3,
  input  [7:0] in_4,
  input  [7:0] in_5,
  input  [31:0] in_6,
  output [31:0] out_7,
  output [31:0] out_8
);

  wire and_1_out, and_2_out, and_3_out, and_4_out, and_5_out, and_6_out, and_7_out, and_8_out;
  wire [31:0] controlled_buffer_1_out, controlled_buffer_2_out, controlled_buffer_3_out,
       controlled_buffer_4_out, controlled_buffer_5_out, controlled_buffer_6_out, controlled_buffer_7_out,
       controlled_buffer_8_out, register_1_q, register_2_q, register_3_q, register_4_q, register_5_q,
       register_6_q, register_7_q, register_8_q;

  assign controlled_buffer_1_out = and_1_out ? in_6 : 32'bz;  // Controlled_Buffer controlled_buffer_1
  and and_1 (and_1_out, 1'b1, in_5[0]);
  assign controlled_buffer_2_out = and_2_out ? in_6 : 32'bz;  // Controlled_Buffer controlled_buffer_2
  and and_2 (and_2_out, 1'b1, in_5[1]);
  assign controlled_buffer_3_out = and_3_out ? in_6 : 32'bz;  // Controlled_Buffer controlled_buffer_3
  and and_3 (and_3_out, 1'b1, in_5[2]);
  assign controlled_buffer_4_out = and_4_out ? in_6 : 32'bz;  // Controlled_Buffer controlled_buffer_4
  and and_4 (and_4_out, 1'b1, in_5[3]);
  assign controlled_buffer_5_out = and_5_out ? in_6 : 32'bz;  // Controlled_Buffer controlled_buffer_5
  and and_5 (and_5_out, 1'b1, in_5[4]);
  assign controlled_buffer_6_out = and_6_out ? in_6 : 32'bz;  // Controlled_Buffer controlled_buffer_6
  and and_6 (and_6_out, 1'b1, in_5[5]);
  assign controlled_buffer_7_out = and_7_out ? in_6 : 32'bz;  // Controlled_Buffer controlled_buffer_7
  and and_7 (and_7_out, 1'b1, in_5[6]);
  assign controlled_buffer_8_out = and_8_out ? in_6 : 32'bz;  // Controlled_Buffer controlled_buffer_8
  and and_8 (and_8_out, 1'b1, in_5[7]);
  Register #(.width(32)) register_1 (
    .D(controlled_buffer_1_out), .en(RegWr), .Q(register_1_q), .clk(Clk));  // open: clr
  Register #(.width(32)) register_2 (
    .D(controlled_buffer_2_out), .en(RegWr), .Q(register_2_q), .clk(Clk));  // open: clr
  Register #(.width(32)) register_3 (
    .D(controlled_buffer_3_out), .en(RegWr), .Q(register_3_q), .clk(Clk));  // open: clr
  Register #(.width(32)) register_4 (
    .D(controlled_buffer_4_out), .en(RegWr), .Q(register_4_q), .clk(Clk));  // open: clr
  Register #(.width(32)) register_5 (
    .D(controlled_buffer_5_out), .en(RegWr), .Q(register_5_q), .clk(Clk));  // open: clr
  Register #(.width(32)) register_6 (
    .D(controlled_buffer_6_out), .en(RegWr), .Q(register_6_q), .clk(Clk));  // open: clr
  Register #(.width(32)) register_7 (
    .D(controlled_buffer_7_out), .en(RegWr), .Q(register_7_q), .clk(Clk));  // open: clr
  Register #(.width(32)) register_8 (
    .D(controlled_buffer_8_out), .en(RegWr), .Q(register_8_q), .clk(Clk));  // open: clr
  assign out_7 = in_3[0] ? register_1_q : 32'bz;  // Controlled_Buffer controlled_buffer_9
  assign out_8 = in_4[0] ? register_1_q : 32'bz;  // Controlled_Buffer controlled_buffer_10
  assign out_7 = in_3[1] ? register_2_q : 32'bz;  // Controlled_Buffer controlled_buffer_11
  assign out_8 = in_4[1] ? register_2_q : 32'bz;  // Controlled_Buffer controlled_buffer_12
  assign out_7 = in_3[2] ? register_3_q : 32'bz;  // Controlled_Buffer controlled_buffer_13
  assign out_8 = in_4[2] ? register_3_q : 32'bz;  // Controlled_Buffer controlled_buffer_14
  assign out_7 = in_3[3] ? register_4_q : 32'bz;  // Controlled_Buffer controlled_buffer_15
  assign out_8 = in_4[3] ? register_4_q : 32'bz;  // Controlled_Buffer controlled_buffer_16
  assign out_7 = in_3[4] ? register_5_q : 32'bz;  // Controlled_Buffer controlled_buffer_17
  assign out_8 = in_4[4] ? register_5_q : 32'bz;  // Controlled_Buffer controlled_buffer_18
  assign out_7 = in_3[5] ? register_6_q : 32'bz;  // Controlled_Buffer controlled_buffer_19
  assign out_8 = in_4[5] ? register_6_q : 32'bz;  // Controlled_Buffer controlled_buffer_20
  assign out_7 = in_3[6] ? register_7_q : 32'bz;  // Controlled_Buffer controlled_buffer_21
  assign out_8 = in_4[6] ? register_7_q : 32'bz;  // Controlled_Buffer controlled_buffer_22
  assign out_7 = in_3[7] ? register_8_q : 32'bz;  // Controlled_Buffer controlled_buffer_23
  assign out_8 = in_4[7] ? register_8_q : 32'bz;  // Controlled_Buffer controlled_buffer_24
endmodule

module AND_logic (
  input  op5,
  input  op4,
  input  op3,
  input  op2,
  input  op1,
  input  op0,
  input  in_7,
  input  in_8,
  input  in_9,
  input  in_10,
  input  in_11,
  input  in_12,
  output out_13,
  output out_14,
  output out_15,
  output out_16,
  output out_17,
  output out_18,
  output out_19,
  output out_20
);

  wire not_1_out, not_2_out, not_3_out, not_4_out, not_5_out, not_6_out, not_7_out, not_8_out, not_9_out,
       not_10_out, not_11_out, not_12_out, R_out;

  not not_1 (not_1_out, op5);
  not not_2 (not_2_out, op4);
  not not_3 (not_3_out, op3);
  not not_4 (not_4_out, op2);
  not not_5 (not_5_out, op1);
  not not_6 (not_6_out, op0);
  and ori (out_13, not_1_out, not_2_out, op3, op2, not_5_out, op0);
  and lw (out_14, op5, not_2_out, not_3_out, not_4_out, op1, op0);
  and sw (out_15, op5, not_2_out, op3, not_4_out, op1, op0);
  and beq (out_16, not_1_out, not_2_out, not_3_out, op2, not_5_out, not_6_out);
  and lui (out_17, not_1_out, not_2_out, op3, op2, op1, op0);
  and R (R_out, not_1_out, not_2_out, not_3_out, not_4_out, not_5_out, not_6_out);
  and lb (out_20, op5, not_2_out, not_3_out, not_4_out, not_5_out, not_6_out);
  not not_7 (not_7_out, in_7);
  not not_8 (not_8_out, in_8);
  not not_9 (not_9_out, in_9);
  not not_10 (not_10_out, in_10);
  not not_11 (not_11_out, in_11);
  not not_12 (not_12_out, in_12);
  and add (out_18, in_7, not_8_out, not_9_out, not_10_out, not_11_out, in_12, R_out);
  and sub (out_19, in_7, not_8_out, not_9_out, not_10_out, in_11, in_11, R_out);
endmodule

module OR_logoc (
  input  lb,
  input  ori,
  input  lw,
  input  sw,
  input  beq,
  input  lui,
  input  add,
  input  in_8,
  output out_9,
  output out_10,
  output out_11,
  output out_12,
  output out_13,
  output out_14,
  output out_15,
  output [2:0] out_16
);

  or RegDst (out_9, add, in_8);
  or AluSrc (out_10, ori, lw, lb, sw, lui);
  or MemtoReg (out_11, lw, lb, sw);
  or RegWrite (out_12, add, in_8, lw, lui, lb);
  or MemWrite (out_13, sw, 1'b0);
  or nPc_sel (out_14, 1'b0, beq);
  or ExtOp (out_15, sw, lb, lw);
  or ALUctr_0 (out_16[0], in_8, beq, lui);
  or ALUctr_1 (out_16[1], ori, lui);
  or ALUctr_2 (out_16[2], 1'b0, 1'b0);

  // Notes on the sheet:
  //   sub
endmodule

module control (
  input  [5:0] in_1,
  input  [5:0] in_2,
  output out_3,
  output out_4,
  output out_5,
  output out_6,
  output out_7,
  output out_8,
  output out_9,
  output [2:0] out_10,
  output out_11
);

  wire and_logic_1_out_13, and_logic_1_out_14, and_logic_1_out_15, and_logic_1_out_16, and_logic_1_out_17,
       and_logic_1_out_18, and_logic_1_out_19;

  AND_logic and_logic_1 (
    .op5(in_1[5]), .op4(in_1[4]), .op3(in_1[3]), .op2(in_1[2]), .op1(in_1[1]), .op0(in_1[0]), .in_7(in_2[5]),
    .in_8(in_2[4]), .in_9(in_2[3]), .in_10(in_2[2]), .in_11(in_2[1]), .in_12(in_2[0]),
    .out_13(and_logic_1_out_13), .out_14(and_logic_1_out_14), .out_15(and_logic_1_out_15),
    .out_16(and_logic_1_out_16), .out_17(and_logic_1_out_17), .out_18(and_logic_1_out_18),
    .out_19(and_logic_1_out_19), .out_20(out_11));
  OR_logoc or_logoc_1 (
    .lb(out_11), .ori(and_logic_1_out_13), .lw(and_logic_1_out_14), .sw(and_logic_1_out_15),
    .beq(and_logic_1_out_16), .lui(and_logic_1_out_17), .add(and_logic_1_out_18), .in_8(and_logic_1_out_19),
    .out_9(out_3), .out_10(out_4), .out_11(out_5), .out_12(out_6), .out_13(out_7), .out_14(out_8),
    .out_15(out_9), .out_16(out_10));

  // Notes on the sheet:
  //   op
  //   funct
endmodule

module DM (
  input  CLK,
  input  MemWrite,
  input  [4:0] in_3,
  input  [31:0] in_4,
  output [31:0] out_5
);

  RAM #(.addrWidth(5), .dataWidth(32), .bus("separate")) ram_1 (
    .addr(in_3), .din(in_4), .data(out_5), .str(MemWrite), .clk(CLK), .ld(1'b1));  // open: sel, clr

  // Notes on the sheet:
  //   Address
  //   DataI
  //   DataO
endmodule

module ALU (
  input  [2:0] in_1,
  input  [31:0] in_2,
  input  [31:0] in_3,
  output [31:0] out_4,
  output out_5
);

  wire and_1_out, and_2_out, and_3_out, and_4_out, not_2_out, not_3_out, not_4_out;
  wire [31:0] aaadd_1_out_3, aaadd_2_out_3, aaadd_3_out_3, bit_extender_1_out, not_1_out, or_1_out;

  assign bit_extender_1_out = {{31{1'b0}}, 1'b1};  // Bit_Extender bit_extender_1
  assign not_1_out = ~in_3;  // NOT_Gate not_1, 32 bits wide
  not not_2 (not_2_out, in_1[0]);
  not not_3 (not_3_out, in_1[1]);
  not not_4 (not_4_out, in_1[2]);
  and and_1 (and_1_out, not_3_out, not_2_out, not_4_out);
  AAADD aaadd_1 (.in_1(not_1_out), .in_2(bit_extender_1_out), .out_3(aaadd_1_out_3));  // open: out_4
  and and_2 (and_2_out, not_4_out, not_3_out, in_1[0]);
  and and_3 (and_3_out, not_4_out, in_1[1], not_2_out);
  and and_4 (and_4_out, not_4_out, in_1[1], in_1[0]);
  AAADD aaadd_2 (.in_1(in_2), .in_2(in_3), .out_3(aaadd_2_out_3));  // open: out_4
  AAADD aaadd_3 (.in_1(in_2), .in_2(aaadd_1_out_3), .out_3(aaadd_3_out_3));  // open: out_4
  assign out_4 = and_1_out ? aaadd_2_out_3 : 32'bz;  // Controlled_Buffer controlled_buffer_1
  assign out_4 = and_2_out ? aaadd_3_out_3 : 32'bz;  // Controlled_Buffer controlled_buffer_2
  assign or_1_out = in_2 | in_3;  // OR_Gate or_1, 32 bits wide
  assign out_4 = and_3_out ? or_1_out : 32'bz;  // Controlled_Buffer controlled_buffer_3
  assign out_4 = and_4_out ? {in_3[15:0], {16{1'b0}}} : 32'bz;  // Controlled_Buffer controlled_buffer_4
  nor nor_1 (out_5, out_4[0], out_4[1], out_4[2], out_4[3], out_4[4], out_4[5], out_4[6], out_4[7], out_4[8], out_4[9], out_4[10], out_4[11], out_4[12], out_4[13], out_4[14], out_4[15], out_4[17], out_4[18], out_4[19], out_4[20], out_4[21], out_4[22], out_4[23], out_4[24], out_4[25], out_4[26], out_4[27], out_4[28], out_4[29], out_4[30], out_4[31], out_4[16]);

  // Notes on the sheet:
  //   ALUctr
  //   A
  //   B
  //   C
  //   Zero
endmodule

module \Reg_32个  (
  input  RegWr,
  input  Clk,
  input  [4:0] in_3,
  input  [4:0] in_4,
  input  [4:0] in_5,
  input  [31:0] in_6,
  output [31:0] out_7,
  output [31:0] out_8
);

  wire [7:0] decoder_1_out0, decoder_1_out8, decoder_1_out16, decoder_1_out24, decoder_2_out0,
       decoder_2_out8, decoder_2_out16, decoder_2_out24, decoder_3_out0, decoder_3_out8, decoder_3_out16,
       decoder_3_out24;

  Decoder #(.select(5), .enable("false")) decoder_1 (
    .out0(decoder_1_out0[0]), .out1(decoder_1_out0[1]), .out2(decoder_1_out0[2]), .out3(decoder_1_out0[3]),
    .out4(decoder_1_out0[4]), .out5(decoder_1_out0[5]), .out6(decoder_1_out0[6]), .out7(decoder_1_out0[7]),
    .out8(decoder_1_out8[0]), .out9(decoder_1_out8[1]), .out10(decoder_1_out8[2]), .out11(decoder_1_out8[3]),
    .out12(decoder_1_out8[4]), .out13(decoder_1_out8[5]), .out14(decoder_1_out8[6]),
    .out15(decoder_1_out8[7]), .out16(decoder_1_out16[0]), .out17(decoder_1_out16[1]),
    .out18(decoder_1_out16[2]), .out19(decoder_1_out16[3]), .out20(decoder_1_out16[4]),
    .out21(decoder_1_out16[5]), .out22(decoder_1_out16[6]), .out23(decoder_1_out16[7]),
    .out24(decoder_1_out24[0]), .out25(decoder_1_out24[1]), .out26(decoder_1_out24[2]),
    .out27(decoder_1_out24[3]), .out28(decoder_1_out24[4]), .out29(decoder_1_out24[5]),
    .out30(decoder_1_out24[6]), .out31(decoder_1_out24[7]), .sel(in_3));
  Decoder #(.select(5), .enable("false")) decoder_2 (
    .out0(decoder_2_out0[0]), .out1(decoder_2_out0[1]), .out2(decoder_2_out0[2]), .out3(decoder_2_out0[3]),
    .out4(decoder_2_out0[4]), .out5(decoder_2_out0[5]), .out6(decoder_2_out0[6]), .out7(decoder_2_out0[7]),
    .out8(decoder_2_out8[0]), .out9(decoder_2_out8[1]), .out10(decoder_2_out8[2]), .out11(decoder_2_out8[3]),
    .out12(decoder_2_out8[4]), .out13(decoder_2_out8[5]), .out14(decoder_2_out8[6]),
    .out15(decoder_2_out8[7]), .out16(decoder_2_out16[0]), .out17(decoder_2_out16[1]),
    .out18(decoder_2_out16[2]), .out19(decoder_2_out16[3]), .out20(decoder_2_out16[4]),
    .out21(decoder_2_out16[5]), .out22(decoder_2_out16[6]), .out23(decoder_2_out16[7]),
    .out24(decoder_2_out24[0]), .out25(decoder_2_out24[1]), .out26(decoder_2_out24[2]),
    .out27(decoder_2_out24[3]), .out28(decoder_2_out24[4]), .out29(decoder_2_out24[5]),
    .out30(decoder_2_out24[6]), .out31(decoder_2_out24[7]), .sel(in_4));
  Decoder #(.select(5), .enable("false")) decoder_3 (
    .out0(decoder_3_out0[0]), .out1(decoder_3_out0[1]), .out2(decoder_3_out0[2]), .out3(decoder_3_out0[3]),
    .out4(decoder_3_out0[4]), .out5(decoder_3_out0[5]), .out6(decoder_3_out0[6]), .out7(decoder_3_out0[7]),
    .out8(decoder_3_out8[0]), .out9(decoder_3_out8[1]), .out10(decoder_3_out8[2]), .out11(decoder_3_out8[3]),
    .out12(decoder_3_out8[4]), .out13(decoder_3_out8[5]), .out14(decoder_3_out8[6]),
    .out15(decoder_3_out8[7]), .out16(decoder_3_out16[0]), .out17(decoder_3_out16[1]),
    .out18(decoder_3_out16[2]), .out19(decoder_3_out16[3]), .out20(decoder_3_out16[4]),
    .out21(decoder_3_out16[5]), .out22(decoder_3_out16[6]), .out23(decoder_3_out16[7]),
    .out24(decoder_3_out24[0]), .out25(decoder_3_out24[1]), .out26(decoder_3_out24[2]),
    .out27(decoder_3_out24[3]), .out28(decoder_3_out24[4]), .out29(decoder_3_out24[5]),
    .out30(decoder_3_out24[6]), .out31(decoder_3_out24[7]), .sel(in_5));
  Reg reg_1 (
    .in_3(decoder_1_out0), .in_4(decoder_2_out0), .in_5(decoder_3_out0), .in_6(in_6), .RegWr(RegWr),
    .Clk(Clk), .out_7(out_7), .out_8(out_8));
  Reg reg_2 (
    .in_3(decoder_1_out8), .in_4(decoder_2_out8), .in_5(decoder_3_out8), .in_6(in_6), .RegWr(RegWr),
    .Clk(Clk), .out_7(out_7), .out_8(out_8));
  Reg reg_3 (
    .in_3(decoder_1_out16), .in_4(decoder_2_out16), .in_5(decoder_3_out16), .in_6(in_6), .RegWr(RegWr),
    .Clk(Clk), .out_7(out_7), .out_8(out_8));
  Reg reg_4 (
    .in_3(decoder_1_out24), .in_4(decoder_2_out24), .in_5(decoder_3_out24), .in_6(in_6), .RegWr(RegWr),
    .Clk(Clk), .out_7(out_7), .out_8(out_8));

  // Notes on the sheet:
  //   WData
endmodule
